// Digital circuit 2's complement.dig as structural Verilog
module _2_s_complement (
  input  n0,
  input  n1,
  input  n2,
  input  n3,
  input  n4,
  input  n5,
  output c0,
  output c1,
  output c2,
  output c3,
  output c4,
  output c5
);

  wire and_1_out, and_2_out, and_3_out, and_4_out, and_5_out, and_6_out, and_7_out, and_8_out, or_1_out,
       or_2_out, or_3_out, or_4_out;

  xor xor_1 (c1, n0, n1);
  or or_1 (or_1_out, n0, n1);
  and and_1 (and_1_out, ~n0, ~n1, n2);  // And
  or or_2 (or_2_out, n0, n1, n2);
  and and_2 (and_2_out, ~n0, ~n1, ~n2, n3);  // And
  or or_3 (or_3_out, n0, n1, n2, n3);
  and and_3 (and_3_out, ~n0, ~n1, ~n2, ~n3, n4);  // And
  or or_4 (or_4_out, n0, n1, n2, n3, n4);
  and and_4 (and_4_out, ~n0, ~n1, ~n2, ~n3, ~n4, n5);  // And
  and and_5 (and_5_out, or_1_out, ~n2);  // And
  and and_6 (and_6_out, or_2_out, ~n3);  // And
  and and_7 (and_7_out, or_3_out, ~n4);  // And
  and and_8 (and_8_out, or_4_out, ~n5);  // And
  or or_5 (c2, and_5_out, and_1_out);
  or or_6 (c3, and_6_out, and_2_out);
  or or_7 (c4, and_7_out, and_3_out);
  or or_8 (c5, and_8_out, and_4_out);

  assign c0 = n0;
endmodule
