// Digital circuit Adder's 6 bits.dig as structural Verilog
module Adder_s_6_bits (
  input  A0,
  input  A1,
  input  A2,
  input  A3,
  input  A4,
  input  A5,
  input  B0,
  input  B1,
  input  B2,
  input  B3,
  input  B4,
  input  B5,
  output s0,
  output s1,
  output s2,
  output s3,
  output s4,
  output s5,
  output F
);

  wire and_1_out, and_2_out, fa_2_co, fa_3_co, fa_4_co, fa_5_co, ha_1_co;

  and and_1 (and_1_out, ~A5, fa_2_co, ~B5);  // And
  or or_1 (F, and_2_out, and_1_out);
  and and_2 (and_2_out, B5, ~fa_2_co, B5);  // And
  FA fa_1 (.A(A5), .B(B5), .Ci(fa_2_co), .S(s5));  // open: Co
  FA fa_2 (.A(A4), .B(B4), .Ci(fa_3_co), .S(s4), .Co(fa_2_co));
  FA fa_3 (.A(A3), .B(B3), .Ci(fa_4_co), .S(s3), .Co(fa_3_co));
  FA fa_4 (.A(A2), .B(B2), .Ci(fa_5_co), .S(s2), .Co(fa_4_co));
  FA fa_5 (.A(A1), .B(B1), .Ci(ha_1_co), .S(s1), .Co(fa_5_co));
  HA ha_1 (.A(A0), .B(B0), .S(s0), .Co(ha_1_co));
endmodule
