// Digital circuit Circuito.dig as structural Verilog
module Circuito (
  input  A3,
  input  A2,
  input  A1,
  input  A0,
  input  O0,
  input  O1,
  input  A4,
  input  A5,
  input  B0,
  input  B1,
  input  B2,
  input  B3,
  input  B4,
  input  B5,
  output s6,
  output s5,
  output s4,
  output s3,
  output s2,
  output s1,
  output s0,
  output s7,
  output F
);

  wire adder_s_6_bits_1_f, adder_s_6_bits_1_s0, adder_s_6_bits_1_s1, adder_s_6_bits_1_s2,
       adder_s_6_bits_1_s3, adder_s_6_bits_1_s4, adder_s_6_bits_1_s5, comparator_s_6_bits_1_s,
       multiplier_s_4_bits_1_f, multiplier_s_4_bits_1_s0, multiplier_s_4_bits_1_s1, multiplier_s_4_bits_1_s2,
       multiplier_s_4_bits_1_s3, multiplier_s_4_bits_1_s4, multiplier_s_4_bits_1_s5,
       multiplier_s_4_bits_1_s6, multiplier_s_4_bits_1_s7, subtractor_s_6_bits_1_f, subtractor_s_6_bits_1_s0,
       subtractor_s_6_bits_1_s1, subtractor_s_6_bits_1_s2, subtractor_s_6_bits_1_s3,
       subtractor_s_6_bits_1_s4, subtractor_s_6_bits_1_s5;

  Mux_without_Comparator mux_without_comparator_1 (
    .E0(adder_s_6_bits_1_f), .E1(subtractor_s_6_bits_1_f), .O0(O0), .O1(O1), .E3(multiplier_s_4_bits_1_f),
    .S(F));
  Multiplier_s_4_bits multiplier_s_4_bits_1 (
    .A0(A0), .A1(A1), .A2(A2), .A3(A3), .A4(A4), .A5(A5), .B0(B0), .B1(B1), .B2(B2), .B3(B3), .B4(B4),
    .B5(B5), .s0(multiplier_s_4_bits_1_s0), .s1(multiplier_s_4_bits_1_s1), .s2(multiplier_s_4_bits_1_s2),
    .s3(multiplier_s_4_bits_1_s3), .s4(multiplier_s_4_bits_1_s4), .s5(multiplier_s_4_bits_1_s5),
    .s6(multiplier_s_4_bits_1_s6), .s7(multiplier_s_4_bits_1_s7), .F(multiplier_s_4_bits_1_f));
  Mux_only_E3__multiplier mux_only_e3__multiplier_1 (.O0(O0), .O1(O1), .E3(multiplier_s_4_bits_1_s7), .S(s7));
  Mux_only_E3__multiplier mux_only_e3__multiplier_2 (.O0(O0), .O1(O1), .E3(multiplier_s_4_bits_1_s6), .S(s6));
  Mux_without_Comparator mux_without_comparator_2 (
    .E0(adder_s_6_bits_1_s5), .E1(subtractor_s_6_bits_1_s5), .O0(O0), .O1(O1), .E3(multiplier_s_4_bits_1_s5),
    .S(s5));
  Comparator_s_6_bits comparator_s_6_bits_1 (
    .A0(A0), .A1(A1), .A2(A2), .A3(A3), .A4(A4), .A5(A5), .B0(B0), .B1(B1), .B2(B2), .B3(B3), .B4(B4),
    .B5(B5), .S(comparator_s_6_bits_1_s));
  Mux_without_Comparator mux_without_comparator_3 (
    .E0(adder_s_6_bits_1_s4), .E1(subtractor_s_6_bits_1_s4), .O0(O0), .O1(O1), .E3(multiplier_s_4_bits_1_s4),
    .S(s4));
  Mux_without_Comparator mux_without_comparator_4 (
    .E0(adder_s_6_bits_1_s3), .E1(subtractor_s_6_bits_1_s3), .O0(O0), .O1(O1), .E3(multiplier_s_4_bits_1_s3),
    .S(s3));
  Subtractor_s_6_bits subtractor_s_6_bits_1 (
    .A0(A0), .A1(A1), .A2(A2), .A3(A3), .A4(A4), .A5(A5), .B0(B0), .B1(B1), .B2(B2), .B3(B3), .B4(B4),
    .B5(B5), .s0(subtractor_s_6_bits_1_s0), .s1(subtractor_s_6_bits_1_s1), .s2(subtractor_s_6_bits_1_s2),
    .s3(subtractor_s_6_bits_1_s3), .s4(subtractor_s_6_bits_1_s4), .s5(subtractor_s_6_bits_1_s5),
    .F(subtractor_s_6_bits_1_f));
  Mux_without_Comparator mux_without_comparator_5 (
    .E0(adder_s_6_bits_1_s2), .E1(subtractor_s_6_bits_1_s2), .O0(O0), .O1(O1), .E3(multiplier_s_4_bits_1_s2),
    .S(s2));
  Mux_without_Comparator mux_without_comparator_6 (
    .E0(adder_s_6_bits_1_s1), .E1(subtractor_s_6_bits_1_s1), .O0(O0), .O1(O1), .E3(multiplier_s_4_bits_1_s1),
    .S(s1));
  Adder_s_6_bits adder_s_6_bits_1 (
    .A0(A0), .A1(A1), .A2(A2), .A3(A3), .A4(A4), .A5(A5), .B0(B0), .B1(B1), .B2(B2), .B3(B3), .B4(B4),
    .B5(B5), .s0(adder_s_6_bits_1_s0), .s1(adder_s_6_bits_1_s1), .s2(adder_s_6_bits_1_s2),
    .s3(adder_s_6_bits_1_s3), .s4(adder_s_6_bits_1_s4), .s5(adder_s_6_bits_1_s5), .F(adder_s_6_bits_1_f));
  Mux mux_1 (
    .E0(adder_s_6_bits_1_s0), .E1(subtractor_s_6_bits_1_s0), .O0(O0), .O1(O1), .E2(comparator_s_6_bits_1_s),
    .E3(multiplier_s_4_bits_1_s0), .S(s0));
endmodule
