// Digital circuit Comparator's 6 bits.dig as structural Verilog
module Comparator_s_6_bits (
  input  A0,
  input  A1,
  input  A2,
  input  A3,
  input  A4,
  input  A5,
  input  B0,
  input  B1,
  input  B2,
  input  B3,
  input  B4,
  input  B5,
  output S
);

  wire comparator_1_s, comparator_2_s, comparator_3_s, comparator_4_s, comparator_5_s, comparator_6_s;

  Comparator comparator_1 (.A(A5), .B(B5), .S(comparator_1_s));
  Comparator comparator_2 (.A(A4), .B(B4), .S(comparator_2_s));
  Comparator comparator_3 (.A(A3), .B(B3), .S(comparator_3_s));
  Comparator comparator_4 (.A(A2), .B(B2), .S(comparator_4_s));
  and and_1 (S, comparator_6_s, comparator_5_s, comparator_4_s, comparator_3_s, comparator_2_s, comparator_1_s);
  Comparator comparator_5 (.A(A1), .B(B1), .S(comparator_5_s));
  Comparator comparator_6 (.A(A0), .B(B0), .S(comparator_6_s));
endmodule
