// Digital circuit Demux.dig as structural Verilog
module Demux (
  input  E,
  input  O,
  output S0,
  output S1
);

  wire not_1_out;

  not not_1 (not_1_out, O);
  and and_1 (S0, E, not_1_out);
  and and_2 (S1, E, O);
endmodule
