// Digital circuit FM.dig as structural Verilog
module FM (
  input  A0,
  input  A1,
  input  A2,
  input  A3,
  input  B,
  output p0,
  output p1,
  output p2,
  output p3
);

  HM hm_1 (.A(A3), .B(B), .P(p3));
  HM hm_2 (.A(A2), .B(B), .P(p2));
  HM hm_3 (.A(A1), .B(B), .P(p1));
  HM hm_4 (.A(A0), .B(B), .P(p0));
endmodule
