// Digital circuit HA B and Cin (for multiplier).dig as structural Verilog
module HA_B_and_Cin__for_multiplier (
  input  B,
  input  Cin,
  output S,
  output Co
);

  xor xor_1 (S, B, Cin);
  and and_1 (Co, B, Cin);
endmodule
