// Digital circuit Multiplier's 4 bits.dig as structural Verilog
module Multiplier_s_4_bits (
  input  A0,
  input  A1,
  input  A2,
  input  A3,
  input  A4,
  input  A5,
  input  B0,
  input  B1,
  input  B2,
  input  B3,
  input  B4,
  input  B5,
  output s0,
  output s1,
  output s2,
  output s3,
  output s4,
  output s5,
  output s6,
  output s7,
  output F
);

  wire demux_1_s0, demux_1_s1, demux_2_s0, demux_2_s1, demux_3_s0, demux_3_s1, demux_4_s0, demux_4_s1,
       demux_5_s0, demux_5_s1, demux_6_s0, demux_6_s1, demux_7_s0, demux_7_s1, demux_8_s0, demux_8_s1,
       fa_1_co, fa_1_s, fa_2_co, fa_2_s, fa_3_co, fa_4_co, fa_5_co, fa_6_co, fa_6_s, fa_7_co, fa_7_s,
       ha_1_co, ha_1_s, ha_2_co, ha_3_co, ha_3_s, ha_b_and_cin__for_multiplier_1_co,
       ha_b_and_cin__for_multiplier_1_s, ha_b_and_cin__for_multiplier_3_co, ha_b_and_cin__for_multiplier_3_s,
       only_a__for_multiplier_1_s, only_a__for_multiplier_4_s, only_cin__for_multiplier_1_s,
       only_cin__for_multiplier_2_s, or_2_out, or_3_out, or_4_out, or_5_out, or_6_out, or_7_out, or_8_out,
       or_9_out, P0_p0, P0_p1, P0_p2, P0_p3, P1_p0, P1_p1, P1_p2, P1_p3, P2_p0, P2_p1, P2_p2, P2_p3, P3_p0,
       P3_p1, P3_p2, P3_p3;

  or or_1 (F, demux_8_s1, demux_7_s1, demux_6_s1, demux_5_s1, demux_4_s1, demux_3_s1, demux_2_s1, demux_1_s1, B5, B4, A4, A5);
  or or_2 (or_2_out, B5, A5, A4, B4);
  Demux demux_1 (.E(B3), .O(or_2_out), .S0(demux_1_s0), .S1(demux_1_s1));
  Demux demux_2 (.E(B2), .O(or_3_out), .S0(demux_2_s0), .S1(demux_2_s1));
  Only_Cin__for_Multiplier only_cin__for_multiplier_1 (
    .Cin(ha_b_and_cin__for_multiplier_1_co), .S(only_cin__for_multiplier_1_s));
  or or_3 (or_3_out, B5, A5, A4, B4);
  HA_B_and_Cin__for_multiplier ha_b_and_cin__for_multiplier_1 (
    .B(P3_p3), .Cin(fa_1_co), .S(ha_b_and_cin__for_multiplier_1_s), .Co(ha_b_and_cin__for_multiplier_1_co));
  or or_4 (or_4_out, B5, A5, A4, B4);
  Demux demux_3 (.E(B1), .O(or_4_out), .S0(demux_3_s0), .S1(demux_3_s1));
  FM P3 (
    .A0(demux_8_s0), .A1(demux_7_s0), .A2(demux_6_s0), .A3(demux_5_s0), .B(demux_1_s0), .p0(P3_p0),
    .p1(P3_p1), .p2(P3_p2), .p3(P3_p3));
  Only_B__for_Multiplier only_b__for_multiplier_1 (.B(only_cin__for_multiplier_1_s), .S(s7));
  or or_5 (or_5_out, B5, A5, A4, B4);
  Demux demux_4 (.E(B0), .O(or_5_out), .S0(demux_4_s0), .S1(demux_4_s1));
  FA fa_1 (.A(P2_p3), .B(P3_p2), .Ci(fa_2_co), .S(fa_1_s), .Co(fa_1_co));
  HA_B_and_Cin__for_multiplier ha_b_and_cin__for_multiplier_2 (
    .B(ha_b_and_cin__for_multiplier_1_s), .Cin(fa_3_co), .S(s6));  // open: Co
  FM P2 (
    .A0(demux_8_s0), .A1(demux_7_s0), .A2(demux_6_s0), .A3(demux_5_s0), .B(demux_2_s0), .p0(P2_p0),
    .p1(P2_p1), .p2(P2_p2), .p3(P2_p3));
  FA fa_2 (.A(P2_p2), .B(P3_p1), .Ci(ha_1_co), .S(fa_2_s), .Co(fa_2_co));
  FA fa_3 (.A(only_cin__for_multiplier_2_s), .B(fa_1_s), .Ci(fa_4_co), .S(s5), .Co(fa_3_co));
  HA ha_1 (.A(P2_p1), .B(P3_p0), .S(ha_1_s), .Co(ha_1_co));
  Only_A__for_Multiplier only_a__for_multiplier_1 (.A(P2_p0), .S(only_a__for_multiplier_1_s));
  FA fa_4 (.A(ha_b_and_cin__for_multiplier_3_s), .B(fa_2_s), .Ci(fa_5_co), .S(s4), .Co(fa_4_co));
  or or_6 (or_6_out, B5, A5, A4, B4);
  Demux demux_5 (.E(A3), .O(or_6_out), .S0(demux_5_s0), .S1(demux_5_s1));
  Only_Cin__for_Multiplier only_cin__for_multiplier_2 (
    .Cin(ha_b_and_cin__for_multiplier_3_co), .S(only_cin__for_multiplier_2_s));
  or or_7 (or_7_out, B5, A5, A4, B4);
  Demux demux_6 (.E(A2), .O(or_7_out), .S0(demux_6_s0), .S1(demux_6_s1));
  HA_B_and_Cin__for_multiplier ha_b_and_cin__for_multiplier_3 (
    .B(P1_p3), .Cin(fa_6_co), .S(ha_b_and_cin__for_multiplier_3_s), .Co(ha_b_and_cin__for_multiplier_3_co));
  FA fa_5 (.A(fa_6_s), .B(ha_1_s), .Ci(ha_2_co), .S(s3), .Co(fa_5_co));
  or or_8 (or_8_out, B5, A5, A4, B4);
  Demux demux_7 (.E(A1), .O(or_8_out), .S0(demux_7_s0), .S1(demux_7_s1));
  FM P1 (
    .A0(demux_8_s0), .A1(demux_7_s0), .A2(demux_6_s0), .A3(demux_5_s0), .B(demux_3_s0), .p0(P1_p0),
    .p1(P1_p1), .p2(P1_p2), .p3(P1_p3));
  FA fa_6 (.A(P0_p3), .B(P1_p2), .Ci(fa_7_co), .S(fa_6_s), .Co(fa_6_co));
  HA ha_2 (.A(fa_7_s), .B(only_a__for_multiplier_1_s), .S(s2), .Co(ha_2_co));
  Only_A__for_Multiplier only_a__for_multiplier_2 (.A(ha_3_s), .S(s1));
  Demux demux_8 (.E(A0), .O(or_9_out), .S0(demux_8_s0), .S1(demux_8_s1));
  Only_A__for_Multiplier only_a__for_multiplier_3 (.A(only_a__for_multiplier_4_s), .S(s0));
  or or_9 (or_9_out, B5, A5, A4, B4);
  FM P0 (
    .A0(demux_8_s0), .A1(demux_7_s0), .A2(demux_6_s0), .A3(demux_5_s0), .B(demux_4_s0), .p0(P0_p0),
    .p1(P0_p1), .p2(P0_p2), .p3(P0_p3));
  FA fa_7 (.A(P0_p2), .B(P1_p1), .Ci(ha_3_co), .S(fa_7_s), .Co(fa_7_co));
  HA ha_3 (.A(P0_p1), .B(P1_p0), .S(ha_3_s), .Co(ha_3_co));
  Only_A__for_Multiplier only_a__for_multiplier_4 (.A(P0_p0), .S(only_a__for_multiplier_4_s));

  // Notes on the sheet:
  //   Soma 2
  //   Resultado (soma 3)
  //   Soma 1
endmodule
