// Digital circuit Mux.dig as structural Verilog
module Mux (
  input  E0,
  input  E1,
  input  O0,
  input  O1,
  input  E2,
  input  E3,
  output S
);

  wire and_1_out, and_2_out, and_3_out, and_4_out;

  and and_1 (and_1_out, ~O1, E0, ~O0);  // And
  and and_2 (and_2_out, O0, E1, ~O1);  // And
  and and_3 (and_3_out, ~O0, E2, O1);  // And
  and and_4 (and_4_out, O0, E3, O1);
  or or_1 (S, and_1_out, and_2_out, and_3_out, and_4_out);
endmodule
