// Digital circuit Subtractor's 6 bits.dig as structural Verilog
module Subtractor_s_6_bits (
  input  A0,
  input  A1,
  input  A2,
  input  A3,
  input  A4,
  input  A5,
  input  B0,
  input  B1,
  input  B2,
  input  B3,
  input  B4,
  input  B5,
  output s0,
  output s1,
  output s2,
  output s3,
  output s4,
  output s5,
  output F
);

  wire _2_s_complement_1_c0, _2_s_complement_1_c1, _2_s_complement_1_c2, _2_s_complement_1_c3,
       _2_s_complement_1_c4, _2_s_complement_1_c5;

  _2_s_complement _2_s_complement_1 (
    .n0(B0), .n1(B1), .n2(B2), .n3(B3), .n4(B4), .n5(B5), .c0(_2_s_complement_1_c0),
    .c1(_2_s_complement_1_c1), .c2(_2_s_complement_1_c2), .c3(_2_s_complement_1_c3),
    .c4(_2_s_complement_1_c4), .c5(_2_s_complement_1_c5));
  Adder_s_6_bits adder_s_6_bits_1 (
    .A0(A0), .A1(A1), .A2(A2), .A3(A3), .A4(A4), .A5(A5), .B0(_2_s_complement_1_c0),
    .B1(_2_s_complement_1_c1), .B2(_2_s_complement_1_c2), .B3(_2_s_complement_1_c3),
    .B4(_2_s_complement_1_c4), .B5(_2_s_complement_1_c5), .s0(s0), .s1(s1), .s2(s2), .s3(s3), .s4(s4),
    .s5(s5), .F(F));
endmodule
