// Digital circuit Reset btn.dig as structural Verilog
module Reset_btn (
  input  D2,
  input  D0,
  input  D2_2,
  input  D3,
  input  D1,
  output R
);

  wire and_1_out, and_2_out;

  and and_1 (and_1_out, D2, D0);
  and and_2 (and_2_out, D2_2, D1);
  or or_1 (R, and_1_out, D3, and_2_out);
endmodule
