// Digital circuit circuito.dig as structural Verilog
module circuito (
  input  clk1,
  input  btn,
  output E0S1,
  output E1S1,
  output ES2,
  output E0S3,
  output E1S3,
  output ES4
);

  wire and_1_out, and_2_out, and_3_out, and_4_out, and_5_out, and_6_out, and_7_out, and_8_out, and_9_out,
       and_10_out, and_11_out, and_12_out, and_13_out, and_14_out, and_15_out, and_16_out, and_17_out,
       and_18_out, and_19_out, clk_slow_1_c_sl, D0_q, D1_q, D2_q, D3_q, latch_s_r_1_q, or_1_out, or_2_out,
       or_3_out, or_4_out, or_5_out, or_6_out, or_7_out, reset_btn_1_r, xnor_1_out, xor_2_out;

  or or_1 (or_1_out, and_1_out, and_2_out);
  or or_2 (or_2_out, and_3_out, and_4_out, and_6_out);
  or or_3 (or_3_out, and_8_out, and_9_out, and_10_out, and_12_out);
  or or_4 (or_4_out, and_14_out, and_16_out, and_17_out, and_18_out);
  D_FF D3 (.D(or_1_out), .C(clk_slow_1_c_sl), .Q(D3_q));  // open: nQ
  D_FF D2 (.D(or_2_out), .C(clk_slow_1_c_sl), .Q(D2_q));  // open: nQ
  D_FF D1 (.D(or_3_out), .C(clk_slow_1_c_sl), .Q(D1_q));  // open: nQ
  D_FF D0 (.D(or_4_out), .C(clk_slow_1_c_sl), .Q(D0_q));  // open: nQ
  clk_slow clk_slow_1 (.clk(clk1), .c_sl(clk_slow_1_c_sl));
  and and_1 (and_1_out, D2_q, ~D1_q, ~D0_q, latch_s_r_1_q);  // And
  Reset_btn reset_btn_1 (.D2(D2_q), .D0(D0_q), .D2_2(D2_q), .D3(D3_q), .D1(D1_q), .R(reset_btn_1_r));
  and and_2 (and_2_out, D2_q, D1_q, D0_q);
  latch_S_R latch_s_r_1 (.S(btn), .E(1'b1), .R(reset_btn_1_r), .Q(latch_s_r_1_q));  // open: nQ
  and and_3 (and_3_out, D2_q, ~D1_q, D0_q);  // And
  and and_4 (and_4_out, ~D2_q, D1_q, D0_q);  // And
  and and_5 (and_5_out, D0_q, D1_q);
  not not_1 (ES2, or_5_out);
  and and_6 (and_6_out, ~D3_q, ~D2_q, latch_s_r_1_q);  // And
  and and_7 (and_7_out, ~D0_q, D2_q);  // And
  or or_5 (or_5_out, D3_q, and_7_out, and_5_out);
  and and_8 (and_8_out, D2_q, ~D1_q, D0_q);  // And
  decoder_interno decoder_interno_1 (.S0(or_6_out), .S1(or_5_out), .S0i(E0S1), .S1i(E1S1));
  and and_9 (and_9_out, ~D1_q, D0_q, ~latch_s_r_1_q);  // And
  and and_10 (and_10_out, ~D2_q, D1_q, latch_s_r_1_q);  // And
  and and_11 (and_11_out, D0_q, ~D1_q, D2_q);  // And
  or or_6 (or_6_out, and_13_out, and_11_out);
  xor xor_1 (ES4, or_7_out, or_5_out);
  and and_12 (and_12_out, D1_q, ~D0_q);  // And
  and and_13 (and_13_out, ~D0_q, D1_q, ~D2_q);  // And
  and and_14 (and_14_out, ~D3_q, ~D2_q, ~D1_q, ~D0_q);  // And
  and and_15 (and_15_out, ~D0_q, ~D2_q);  // And
  and and_16 (and_16_out, D2_q, D1_q, ~D0_q);  // And
  or or_7 (or_7_out, xor_2_out, and_15_out);
  and and_17 (and_17_out, D1_q, ~D0_q, ~latch_s_r_1_q);  // And
  xor xor_2 (xor_2_out, D0_q, D1_q);
  decoder_interno decoder_interno_2 (.S0(and_19_out), .S1(or_7_out), .S0i(E0S3), .S1i(E1S3));
  and and_18 (and_18_out, ~D2_q, D0_q, latch_s_r_1_q);  // And
  and and_19 (and_19_out, xnor_1_out, D2_q);
  xnor xnor_1 (xnor_1_out, D0_q, D1_q);

  // Notes on the sheet:
  //   D3t+1
  //   D2t+1
  //   D1t+1
  //   D0t+1
  //   Reset+Btn+Manter Btn
  //   Calc S1(1)
  //   Calc S2
  //   Calc S1(0)
  //   Decoder para 
  //   trocar para a 
  //   convenção 
  //   usada no 
  //   main
  //   Calc S4
  //   Calc S3(1)
  //   Calc S3(0)
endmodule
