// Digital circuit clk slow.dig as structural Verilog
module clk_slow (
  input  clk,
  output c_sl
);

  wire d_ff_1_nq, d_ff_2_nq;

  D_FF d_ff_1 (.D(d_ff_1_nq), .C(clk), .nQ(d_ff_1_nq));  // open: Q
  D_FF d_ff_2 (.D(d_ff_2_nq), .C(d_ff_1_nq), .Q(c_sl), .nQ(d_ff_2_nq));
endmodule
