// Digital circuit decoder_interno.dig as structural Verilog
module decoder_interno (
  input  S0,
  input  S1,
  output S0i,
  output S1i
);

  and and_1 (S1i, ~S1, ~S0);  // And

  assign S0i = S0;
endmodule
